// Logisim project Avance Practica4.circ as structural Verilog: 6 circuits, main circuit Sumador_1_bit
module Sumador_1_bit (
  input  C_in,
  input  A,
  input  B,
  output Suma,
  output Carry_Out
);

  wire and_1_out, and_2_out, xor_1_out;

  xor xor_1 (xor_1_out, A, B);
  and and_1 (and_1_out, A, B);
  xor xor_2 (Suma, C_in, xor_1_out);
  and and_2 (and_2_out, C_in, xor_1_out);
  or or_1 (Carry_Out, and_2_out, and_1_out);

  // Notes on the sheet:
  //   Full Adder Ejercicio 1
endmodule

module Sumador_8_bit (
  input  [7:0] in_1,
  input  C,
  input  [7:0] in_3,
  output [7:0] out_4
);

  wire sumador_1_bit_1_carry_out, sumador_1_bit_2_carry_out, sumador_1_bit_3_carry_out,
       sumador_1_bit_4_carry_out, sumador_1_bit_5_carry_out, sumador_1_bit_6_carry_out,
       sumador_1_bit_7_carry_out;

  Sumador_1_bit sumador_1_bit_1 (
    .C_in(C), .A(in_1[0]), .B(in_3[0]), .Suma(out_4[0]), .Carry_Out(sumador_1_bit_1_carry_out));
  Sumador_1_bit sumador_1_bit_2 (
    .C_in(sumador_1_bit_1_carry_out), .A(in_1[1]), .B(in_3[1]), .Suma(out_4[1]),
    .Carry_Out(sumador_1_bit_2_carry_out));
  Sumador_1_bit sumador_1_bit_3 (
    .C_in(sumador_1_bit_2_carry_out), .A(in_1[2]), .B(in_3[2]), .Suma(out_4[2]),
    .Carry_Out(sumador_1_bit_3_carry_out));
  Sumador_1_bit sumador_1_bit_4 (
    .C_in(sumador_1_bit_3_carry_out), .A(in_1[3]), .B(in_3[3]), .Suma(out_4[3]),
    .Carry_Out(sumador_1_bit_4_carry_out));
  Sumador_1_bit sumador_1_bit_5 (
    .C_in(sumador_1_bit_4_carry_out), .A(in_1[4]), .B(in_3[4]), .Suma(out_4[4]),
    .Carry_Out(sumador_1_bit_5_carry_out));
  Sumador_1_bit sumador_1_bit_6 (
    .C_in(sumador_1_bit_5_carry_out), .A(in_1[5]), .B(in_3[5]), .Suma(out_4[5]),
    .Carry_Out(sumador_1_bit_6_carry_out));
  Sumador_1_bit sumador_1_bit_7 (
    .C_in(sumador_1_bit_6_carry_out), .A(in_1[6]), .B(in_3[6]), .Suma(out_4[6]),
    .Carry_Out(sumador_1_bit_7_carry_out));
  Sumador_1_bit sumador_1_bit_8 (
    .C_in(sumador_1_bit_7_carry_out), .A(in_1[7]), .B(in_3[7]), .Suma(out_4[7]));  // open: Carry_Out

  // Notes on the sheet:
  //   A
  //   B
  //   Sumador de 8bits
endmodule

module Ejercicio_3 (
  input  in_1,
  input  [7:0] in_2,
  input  [7:0] in_3,
  input  in_4,
  output [7:0] out_5
);

  wire [7:0] restador_8bits_out_4, sumador_8_bit_out_4;

  Sumador_8_bit sumador_8_bit (.in_1(in_2), .C(in_1), .in_3(in_3), .out_4(sumador_8_bit_out_4));
  restador_8bits restador_8bits (.in_1(in_2), .C(in_1), .in_3(in_3), .out_4(restador_8bits_out_4));
  Multiplexer #(.width(8), .enable("false")) multiplexer_1 (
    .in0(sumador_8_bit_out_4), .in1(restador_8bits_out_4), .out(out_5), .sel(in_4));
endmodule

module restador (
  input  C_in,
  input  A,
  input  B,
  output Resta,
  output Carry_Out
);

  wire and_1_out, and_2_out, not_1_out, xor_1_out;

  not not_1 (not_1_out, A);
  xor xor_1 (xor_1_out, A, B);
  and and_1 (and_1_out, not_1_out, B);
  xor xor_2 (Resta, C_in, xor_1_out);
  and and_2 (and_2_out, C_in, xor_1_out);
  or or_1 (Carry_Out, and_2_out, and_1_out);
endmodule

module restador_8bits (
  input  [7:0] in_1,
  input  C,
  input  [7:0] in_3,
  output [7:0] out_4
);

  wire restador_1_carry_out, restador_2_carry_out, restador_3_carry_out, restador_4_carry_out,
       restador_5_carry_out, restador_6_carry_out, restador_7_carry_out;

  restador restador_1 (.C_in(C), .A(in_1[0]), .B(in_3[0]), .Resta(out_4[0]), .Carry_Out(restador_1_carry_out));
  restador restador_2 (
    .C_in(restador_1_carry_out), .A(in_1[1]), .B(in_3[1]), .Resta(out_4[1]), .Carry_Out(restador_2_carry_out));
  restador restador_3 (
    .C_in(restador_2_carry_out), .A(in_1[2]), .B(in_3[2]), .Resta(out_4[2]), .Carry_Out(restador_3_carry_out));
  restador restador_4 (
    .C_in(restador_3_carry_out), .A(in_1[3]), .B(in_3[3]), .Resta(out_4[3]), .Carry_Out(restador_4_carry_out));
  restador restador_5 (
    .C_in(restador_4_carry_out), .A(in_1[4]), .B(in_3[4]), .Resta(out_4[4]), .Carry_Out(restador_5_carry_out));
  restador restador_6 (
    .C_in(restador_5_carry_out), .A(in_1[5]), .B(in_3[5]), .Resta(out_4[5]), .Carry_Out(restador_6_carry_out));
  restador restador_7 (
    .C_in(restador_6_carry_out), .A(in_1[6]), .B(in_3[6]), .Resta(out_4[6]), .Carry_Out(restador_7_carry_out));
  restador restador_8 (.C_in(restador_7_carry_out), .A(in_1[7]), .B(in_3[7]), .Resta(out_4[7]));  // open: Carry_Out

  // Notes on the sheet:
  //   A
  //   B
  //   Restador de 8bits
endmodule

module Ejercicio4 (
  input  in_1,
  input  [3:0] in_2,
  input  [3:0] in_3,
  input  [2:0] in_4,
  input  [3:0] in_5,
  input  [3:0] in_6,
  input  [3:0] in_7,
  input  [3:0] in_8,
  input  [2:0] in_9,
  output [3:0] out_10,
  output [3:0] out_11
);

  wire [3:0] adder_1_out, subtractor_1_out;

  Adder #(.width(4)) adder_1 (.a(in_2), .b(in_3), .out(adder_1_out));  // open: cin, cout
  Subtractor #(.width(4)) subtractor_1 (.a(in_2), .b(in_3), .out(subtractor_1_out));  // open: bin, bout
  Multiplexer #(.select(3), .width(4)) multiplexer_1 (
    .in0(adder_1_out), .in1(subtractor_1_out), .out(out_10), .sel(in_4));  // open: in2, in3, in4, in5, in6, in7, en
  Multiplexer #(.select(3), .width(4)) multiplexer_2 (
    .in0(in_5), .in1(in_6), .in2(in_7), .in3(in_8), .out(out_11), .sel(in_9));  // open: in4, in5, in6, in7, en

  // Notes on the sheet:
  //   in_8: pull=down
  //   in_7: pull=down
  //   in_6: pull=down
  //   in_3: pull=down
endmodule
